// Logisim project ex4.circ as structural Verilog: 5 circuits, main circuit rot2
module RotRight (
  input  [15:0] INPUT0,
  input  [3:0] AMOUNT,
  output [15:0] OUTPUT0
);

  wire [15:0] rot1_1_out_2, rot2_1_out_2, rot4_1_out_2, rot8_1_out_2, TUN1, TUN2, TUN3;

  rot1 rot1_1 (.in_1(INPUT0), .out_2(rot1_1_out_2));
  rot2 rot2_1 (.in_1(TUN1), .out_2(rot2_1_out_2));
  rot4 rot4_1 (.in_1(TUN2), .out_2(rot4_1_out_2));
  rot8 rot8_1 (.in_1(TUN3), .out_2(rot8_1_out_2));
  Multiplexer #(.width(16)) multiplexer_1 (.in0(INPUT0), .in1(rot1_1_out_2), .out(TUN1), .sel(AMOUNT[0]));
  Multiplexer #(.width(16)) multiplexer_2 (.in0(TUN1), .in1(rot2_1_out_2), .out(TUN2), .sel(AMOUNT[1]));
  Multiplexer #(.width(16)) multiplexer_3 (.in0(TUN2), .in1(rot4_1_out_2), .out(TUN3), .sel(AMOUNT[2]));
  Multiplexer #(.width(16)) multiplexer_4 (.in0(TUN3), .in1(rot8_1_out_2), .out(OUTPUT0), .sel(AMOUNT[3]));

  // Other names for the same wires on the sheet: Sel0 = AMOUNT[0]; Sel1 = AMOUNT[1]; Sel2 = AMOUNT[2];
  //   Sel3 = AMOUNT[3]; TUN0[15:0] = INPUT0; TUN4[15:0] = OUTPUT0
endmodule

module rot1 (
  input  [15:0] in_1,
  output [15:0] out_2
);


  assign out_2 = {in_1[0], in_1[15:1]};
endmodule

module rot2 (
  input  [15:0] in_1,
  output [15:0] out_2
);


  assign out_2 = {in_1[1:0], in_1[15:2]};
endmodule

module rot4 (
  input  [15:0] in_1,
  output [15:0] out_2
);


  assign out_2 = {in_1[3:0], in_1[15:4]};
endmodule

module rot8 (
  input  [15:0] in_1,
  output [15:0] out_2
);


  assign out_2 = {in_1[7:0], in_1[15:8]};
endmodule
